# Fritzing sketch High Level Controller (saved by Fritzing 0.8.7b)
breadboards: 1

parts:
  Part1 = Arduino Nano (Rev3.0)
  Power_plug1 = Power plug
  IC1 = IC, DIP package, 16 pins [chip_label=ULN2069B]
  IC2 = IC, DIP package, 16 pins [chip_label=ULN2069B]
  D1 = Schottky Diode [part_number=1N5817 package="300 mil [THT]"]
  D2 = Schottky Diode [part_number=1N5817 package="300 mil [THT]"]
  D3 = Schottky Diode [part_number=1N5817 package="300 mil [THT]"]
  D4 = Schottky Diode [part_number=1N5817 package="300 mil [THT]"]
  D5 = Schottky Diode [part_number=1N5817 package="300 mil [THT]"]  # not connected
  D6 = Schottky Diode [part_number=1N5817 package="300 mil [THT]"]  # not connected
  D7 = Schottky Diode [part_number=1N5817 package="300 mil [THT]"]
  D8 = Schottky Diode [part_number=1N5817 package="300 mil [THT]"]

nets:
  N1: Part1.D9, IC2.pin3
  N2: Part1.D10, IC2.pin6
  N3: Part1.D11/MOSI, IC1.pin3
  N4: Part1.D12/MISO, IC1.pin6
  N5: Part1.A0, IC2.pin15
  N6: Part1.AREF, IC2.pin11
  N7: Part1.3V3, IC1.pin11
  N8: Part1.D13/SCK, IC1.pin15
  N9: Power_plug1.GND, IC1.pin4, IC1.pin5, IC1.pin12, IC1.pin13, IC2.pin4, IC2.pin5, IC2.pin12, IC2.pin13, IC2.pin14
  N10: Power_plug1.VCC, IC1.pin14, D1.cathode, D2.cathode, D3.cathode, D4.cathode, D7.cathode, D8.cathode
  N11: IC1.pin2, D7.anode
  N12: IC1.pin8, D8.anode
  N13: IC1.pin10, D4.anode
  N14: IC1.pin16, D3.anode
  N15: IC2.pin10, D2.anode
  N16: IC2.pin16, D1.anode
